// Digital circuit Test_AddressDecodingLogic.dig as structural Verilog
module Test_AddressDecodingLogic (
  input  PHI2,
  input  [15:0] ADDR,
  output CS,
  output OE,
  output CS2,
  output OE_2,
  output CE,
  output CS1,
  output CS1_2,
  output CS0
);

  nand nand_1 (CE, ADDR[15], ADDR[15]);
  nand nand_2 (CS, PHI2, CE);
  nand nand_3 (CS1_2, CE, ADDR[14]);

  assign CS0 = ADDR[9];
  assign CS1 = ADDR[13];
  assign CS2 = CS1_2;
  assign OE = ADDR[14];
  assign OE_2 = CE;

  // Notes on the sheet:
  //   RAM
  //   ROM
  //   6522
  //   6551
endmodule
